# Fritzing sketch SmartSwitch (saved by Fritzing 0.9.3b)
breadboards: 1

parts:
  R1 = Resistor [tolerance=±5% resistance=220 package=THT]
  Raspberry_Pi_2 = Raspberry Pi 3 [part_number=RPI-3-V1.2]
  U1 = 4-Channel 5v Relay Shield [package=relay-4ch5v10a]
  LED1 = LED - 5mm [color="Red (633nm)" package="5 mm [THT]"]
  LED2 = LEDs [package=led10mm]
  F1 = Fan - Ventilador [package=THT]

nets:
  N1: R1.Pin_0, LED1.cathode
  GND: R1.Pin_1, Raspberry_Pi_2.GND, U1.GND
  N2: Raspberry_Pi_2.GIPO5, U1.IN1
  N3: Raspberry_Pi_2.GIPO6, LED1.anode
  N4: Raspberry_Pi_2.GIPO16, U1.IN2
  5V: Raspberry_Pi_2.5V, U1.VCC, U1.IN4
  N5: U1.K1-In, LED2.A
  N6: U1.K2-In, F1.5V

custom parts:
  4-Channel 5v Relay Shield: 4 Channel 5v Relay Shield w. 2x SPD-06VDC-SD-C
  LEDs: LEDs Standard schematic elements and footprints for 5mm, 3mm, 1206, and 0603 sized LEDs. 5mm - Spark Fun Electronics SKU : COM-00529 (and others)
  Fan - Ventilador: Ventilador de 2 pines, se encuentra comunmente en computadoras de escritorio
